// Logisim project Ekran.circ as structural Verilog: 1 circuit, main circuit main
module main (
  input  [19:0] in_1,
  input  in_2
);

  wire clock_1_out, counter_1_carry, keyboard_1_avail, main_2_p2, main_2_p3, main_3_p4, main_3_p5, main_3_p6,
       main_3_p7, main_3_p8, main_3_p9, main_3_p10, main_3_p11, main_3_p12, main_3_p13, main_3_p14,
       main_3_p15, main_3_p16, main_3_p17, main_3_p18, main_3_p19, main_3_p20, main_3_p21, main_3_p22,
       main_3_p23, not_1_out, register_1_q;
  wire [4:0] main_1_out_2, main_1_out_3;
  wire [6:0] keyboard_1_data;
  wire [19:0] main_4_p41, main_4_p42, main_4_p43, main_4_p44, main_4_p45, main_4_p46, main_4_p47, main_4_p48,
       main_4_p49, main_4_p50, main_4_p51, main_4_p52, main_4_p53, main_4_p54, main_4_p55, main_4_p56,
       main_4_p57, main_4_p58, main_4_p59, main_4_p60, shifter_1_out, shifter_2_out;

  Keyboard keyboard_1 (
    .re(1'b1), .clr(keyboard_1_avail), .avail(keyboard_1_avail), .data(keyboard_1_data));  // open: clk
  Clock clock_1 (.out(clock_1_out));
  Counter #(.max('h64)) counter_1 (.carry(counter_1_carry), .clk(clock_1_out));  // open: load, D, count, Q, clr
  LR_main main_1 (.in_1(keyboard_1_data), .out_2(main_1_out_2), .out_3(main_1_out_3));
  // Enter_Up_Down_main main_2: pin names not known; wires that end beside it: keyboard_1_data, main_2_p2, main_2_p3
  Counter counter_2 (.clk(counter_1_carry));  // open: load, D, count, Q, carry, clr
  not not_1 (not_1_out, in_2);
  Shifter #(.width(20)) shifter_1 (.in(20'h200), .\dist (main_1_out_2), .out(shifter_1_out));
  Register #(.width(1), .trigger("high")) register_1 (
    .D(clock_1_out), .Q(register_1_q), .clk(not_1_out), .clr(in_2));  // open: en
  Shifter #(.width(20), .shift("lr")) shifter_2 (.in(shifter_1_out), .\dist (main_1_out_3), .out(shifter_2_out));
  // Uu_Down32_main main_3: pin names not known; wires that end beside it: main_2_p3, shifter_2_out, register_1_q, main_3_p4, main_3_p5, main_3_p6, main_3_p7, main_3_p8, main_3_p9, main_3_p10, main_3_p11, main_3_p12, main_3_p13, main_3_p14, main_3_p15, main_3_p16, main_3_p17, main_3_p18, main_3_p19, main_3_p20, main_3_p21, main_3_p22, main_3_p23
  DotMatrix #(.inputtype("row"), .matrixcols(20), .matrixrows(20)) dotmatrix_1 (
    .row0(main_4_p41), .row1(main_4_p42), .row2(main_4_p43), .row3(main_4_p44), .row4(main_4_p45),
    .row5(main_4_p46), .row6(main_4_p47), .row7(main_4_p48), .row8(main_4_p49), .row9(main_4_p50),
    .row10(main_4_p51), .row11(main_4_p52), .row12(main_4_p53), .row13(main_4_p54), .row14(main_4_p55),
    .row15(main_4_p56), .row16(main_4_p57), .row17(main_4_p58), .row18(main_4_p59), .row19(main_4_p60));
  // Register32x32_main main_4: pin names not known; wires that end beside it: main_3_p4, main_3_p5, main_3_p6, main_3_p7, main_3_p8, main_3_p9, main_3_p10, main_3_p11, main_3_p12, main_3_p13, main_3_p14, main_3_p15, main_3_p16, main_3_p17, main_3_p18, main_3_p19, main_3_p20, main_3_p21, main_3_p22, main_3_p23, in_1, in_1, in_1, in_1, in_1, in_1, in_1, in_1, in_1, in_1, in_1, in_1, in_1, in_1, in_1, in_1, in_1, in_1, in_1, in_1, main_4_p41, main_4_p42, main_4_p43, main_4_p44, main_4_p45, main_4_p46, main_4_p47, main_4_p48, main_4_p49, main_4_p50, main_4_p51, main_4_p52, main_4_p53, main_4_p54, main_4_p55, main_4_p56, main_4_p57, main_4_p58, main_4_p59, main_4_p60
endmodule
